// Digital circuit RISCV.dig as structural Verilog
module RISCV (
  input  [31:0] in_1,
  input  [31:0] in_2,
  input  in_3,
  input  [31:0] in_5,
  input  [31:0] in_6,
  input  [31:0] in_8,
  input  [1:0] in_9,
  output [31:0] out_4,
  output [31:0] out_7
);

  MUX_2inputs #(.applicationType("GHDL")) u_MUX_2inputs (
    .enter1(in_1), .enter2(in_2), .selector(in_3), .\output (out_4));
  MUX_3inputs #(.applicationType("GHDL")) u_MUX_3inputs (
    .enter1(in_5), .enter2(in_6), .enter3(in_8), .selector(in_9), .\output (out_7));
endmodule

/* Code of MUX_2inputs:
LIBRARY ieee;
USE ieee.std_logic_1164.all;

ENTITY MUX_2inputs IS
	PORT(
		enter1, enter2 : IN STD_LOGIC_VECTOR (31 downto 0);
		selector : IN STD_LOGIC;
		output : OUT STD_LOGIC_VECTOR (31 downto 0)
	);
END MUX_2inputs;

ARCHITECTURE MUX_logic OF MUX_2inputs IS
	BEGIN
		output <= enter1 WHEN selector = '0' ELSE
			enter2;

	END MUX_logic;
--------------------------------------------------------------------------------
*/

/* Code of MUX_3inputs:
LIBRARY ieee;
USE ieee.std_logic_1164.all;

ENTITY MUX_3inputs IS
	PORT(
		enter1, enter2, enter3 : IN STD_LOGIC_VECTOR (31 downto 0);
		selector: IN STD_LOGIC_VECTOR (1 downto 0);
		output : OUT STD_LOGIC_VECTOR (31 downto 0)
	);
END MUX_3inputs;

ARCHITECTURE MUX_logic OF MUX_3inputs IS
	BEGIN
		output <= enter1 WHEN selector = "00" ELSE
			enter2 WHEN selector = "01" ELSE
			enter3;

	END MUX_logic;
--------------------------------------------------------------------------------
*/
